# Fritzing sketch laser_shark_sketch (saved by Fritzing 0.9.3b)
breadboards: 1

parts:
  Part2 = Arduino Uno (Rev3) - ICSP
  hc-sr2 = hc-sr04
  S2 = H-Bridge with L298N
  VCC2 = 4 x AAA Battery Mount
  R2 = Resistor [tolerance=±5% resistance=1k package=THT]
  M3 = DC Motor
  M4 = DC Motor
  LED1 = smd LED [color="Red (633nm)" package="0603 [SMD]"]
  R3 = Resistor [tolerance=±5% resistance=1k package=THT]
  R4 = Resistor [tolerance=±5% resistance=1k package=THT]
  R5 = Resistor [tolerance=±5% resistance=1k package=THT]
  LED2 = smd LED [color="White (4500K)" package="0603 [SMD]"]
  LED3 = smd LED [color="Infrared (940nm)" package="0603 [SMD]"]
  LED4 = smd LED [color="Infrared (940nm)" package="0603 [SMD]"]
  LED5 = smd LED [color="Infrared (940nm)" package="0603 [SMD]"]
  LD1 = LD
  J1 = Piezo Speaker

nets:
  N1: Part2.A0, R5.Pin_1, LED3.anode, LED4.anode, LED5.anode
  N2: Part2.D8, S2.IN2
  N3: Part2.D9_PWM, S2.IN1
  N4: Part2.D10_PWM/SS, R2.Pin_0
  N5: Part2.D11_PWM/MOSI, hc-sr2.Trig
  N6: Part2.D2, R4.Pin_0
  N7: Part2.D3_PWM, S2.IN4
  N8: Part2.D4, S2.IN3
  N9: Part2.D7, LED1.anode
  N10: Part2.3V3, R3.Pin_1
  5V: Part2.5V, hc-sr2.VCC, S2.5V, LED3.cathode, LED4.cathode, LED5.cathode, LD1.anode
  GND: Part2.GND, hc-sr2.GND, S2.GND, VCC2.-, LED1.cathode, R5.Pin_0, LED2.cathode, LD1.cathode, J1.pin1
  N11: hc-sr2.Echo, R2.Pin_1
  N12: S2.12V, VCC2.+
  N13: S2.M1-01, M3.pin_2
  N14: S2.M1-02, M3.pin_1
  N15: S2.M2-01, M4.pin_2
  N16: S2.M2-02, M4.pin_1
  N17: R3.Pin_0, LED2.anode
  N18: R4.Pin_1, J1.pin2

custom parts:
  H-Bridge with L298N: h-bridge
  LD: A Generic Red Dot Laser Diode Module (~5mW)
